// Logisim project Animacja-ekranu.circ as structural Verilog: 1 circuit, main circuit main
module main (
);

  wire button_1_out, button_2_out, clock_1_out, main_1_p4;
  wire [23:0] random_1_out, shift_register_1_out, shift_register_1_q0, shift_register_1_q1,
       shift_register_1_q2, shift_register_1_q3, shift_register_1_q4, shift_register_1_q5,
       shift_register_1_q6, shift_register_1_q7, shift_register_2_q0, shift_register_2_q1,
       shift_register_2_q2, shift_register_2_q3, shift_register_2_q4, shift_register_2_q5,
       shift_register_2_q6, shift_register_2_q7;

  Clock clock_1 (.out(clock_1_out));
  Button button_1 (.out(button_1_out));
  Button button_2 (.out(button_2_out));
  // Stop_countera_main main_1: pin names not known; wires that end beside it: clock_1_out, button_1_out, 5'b00111, main_1_p4
  Random #(.width(24)) random_1 (.clk(main_1_p4), .out(random_1_out));  // open: next, clr
  Shift_Register #(.width(24)) shift_register_1 (
    .in(random_1_out), .clk(main_1_p4), .out(shift_register_1_out), .clr(button_2_out),
    .q0(shift_register_1_q0), .q1(shift_register_1_q1), .q2(shift_register_1_q2), .q3(shift_register_1_q3),
    .q4(shift_register_1_q4), .q5(shift_register_1_q5), .q6(shift_register_1_q6), .q7(shift_register_1_q7));  // open: shift, load, d0, d1, d2, d3, d4, d5, d6, d7
  Shift_Register #(.width(24)) shift_register_2 (
    .in(shift_register_1_out), .clk(main_1_p4), .clr(button_2_out), .q0(shift_register_2_q0),
    .q1(shift_register_2_q1), .q2(shift_register_2_q2), .q3(shift_register_2_q3), .q4(shift_register_2_q4),
    .q5(shift_register_2_q5), .q6(shift_register_2_q6), .q7(shift_register_2_q7));  // open: shift, out, load, d0, d1, d2, d3, d4, d5, d6, d7
  DotMatrix #(.inputtype("row"), .matrixcols(24), .matrixrows(8)) dotmatrix_1 (
    .row0(shift_register_1_q0), .row1(shift_register_1_q1), .row2(shift_register_1_q2),
    .row3(shift_register_1_q3), .row4(shift_register_1_q4), .row5(shift_register_1_q5),
    .row6(shift_register_1_q6), .row7(shift_register_1_q7));
  DotMatrix #(.inputtype("row"), .matrixcols(24), .matrixrows(8)) dotmatrix_2 (
    .row0(shift_register_2_q0), .row1(shift_register_2_q1), .row2(shift_register_2_q2),
    .row3(shift_register_2_q3), .row4(shift_register_2_q4), .row5(shift_register_2_q5),
    .row6(shift_register_2_q6), .row7(shift_register_2_q7));
endmodule
