// Logisim project PointCounter.circ as structural Verilog: 1 circuit, main circuit main
module main (
  input  ADD,
  input  RESET,
  output LIMIT,
  output [3:0] X000,
  output [3:0] _0X00,
  output [3:0] _00X0,
  output [3:0] _000X,
  output [13:0] Current_value
);

  wire and_1_out, comparator_1_lt;
  wire [13:0] divider_1_out, divider_2_rem, divider_3_out, divider_4_rem, divider_5_out, divider_6_rem;

  Comparator #(.width(14), .mode("unsigned")) comparator_1 (
    .a(Current_value), .b(14'h270f), .eq(LIMIT), .lt(comparator_1_lt));  // open: gt
  and and_1 (and_1_out, comparator_1_lt, ADD);
  Counter #(.width(14), .max('h3fff)) counter_1 (
    .count(and_1_out), .Q(Current_value), .clk(and_1_out), .clr(RESET));  // open: load, D, carry
  Divider #(.width(14)) divider_1 (.a(Current_value), .b(14'h3e8), .out(divider_1_out));  // open: upper, rem
  BitSelector #(.width(14), .group(4)) bitselector_1 (.in(divider_1_out), .out(X000), .sel(2'b00));
  Divider #(.width(14)) divider_2 (.a(Current_value), .b(14'h3e8), .rem(divider_2_rem));  // open: out, upper
  Divider #(.width(14)) divider_3 (.a(divider_2_rem), .b(14'h64), .out(divider_3_out));  // open: upper, rem
  Divider #(.width(14)) divider_4 (.a(Current_value), .b(14'h64), .rem(divider_4_rem));  // open: out, upper
  Divider #(.width(14)) divider_5 (.a(divider_4_rem), .b(14'ha), .out(divider_5_out));  // open: upper, rem
  BitSelector #(.width(14), .group(4)) bitselector_2 (.in(divider_3_out), .out(_0X00), .sel(2'b00));
  Divider #(.width(14)) divider_6 (.a(Current_value), .b(14'ha), .rem(divider_6_rem));  // open: out, upper
  BitSelector #(.width(14), .group(4)) bitselector_3 (.in(divider_5_out), .out(_00X0), .sel(2'b00));
  BitSelector #(.width(14), .group(4)) bitselector_4 (.in(divider_6_rem), .out(_000X), .sel(2'b00));
endmodule
