// Logisim project ScoreHolder.circ as structural Verilog: 1 circuit, main circuit main
module main (
  input  [13:0] CurrentPoints,
  input  RESET,
  input  CLK,
  output [3:0] X000,
  output [3:0] _0X00,
  output [3:0] _00X0,
  output [3:0] _000X
);

  wire and_1_out, comparator_1_gt, main_1_tics_out, not_1_out, not_2_out;
  wire [13:0] controlled_buffer_2_out, divider_1_out, divider_2_rem, divider_3_out, divider_4_rem,
       divider_5_out, divider_6_rem, ram_1_data, register_1_q;

  not not_1 (not_1_out, main_1_tics_out);
  RAM #(.addrWidth(2), .dataWidth(14), .bus("asynch")) ram_1 (
    .addr(2'b00), .data(ram_1_data), .ld(not_1_out), .clr(RESET));  // open: sel
  assign ram_1_data = main_1_tics_out ? CurrentPoints : 14'bz;  // Controlled_Buffer controlled_buffer_1
  and and_1 (and_1_out, CLK, comparator_1_gt);
  Comparator #(.width(14), .mode("unsigned")) comparator_1 (
    .a(CurrentPoints), .b(register_1_q), .gt(comparator_1_gt));  // open: eq, lt
  not not_2 (not_2_out, main_1_tics_out);
  assign controlled_buffer_2_out = not_2_out ? ram_1_data : 14'bz;  // Controlled_Buffer controlled_buffer_2
  Stop_countera_main main_1 (
    .CLK(and_1_out), .Reset(comparator_1_gt), .Number_of_tics(5'b00010), .Tics_out(main_1_tics_out));
  Register #(.width(14)) register_1 (
    .D(controlled_buffer_2_out), .Q(register_1_q), .clk(main_1_tics_out), .clr(RESET));  // open: en
  Divider #(.width(14)) divider_1 (.a(register_1_q), .b(14'h3e8), .out(divider_1_out));  // open: upper, rem
  BitSelector #(.width(14), .group(4)) bitselector_1 (.in(divider_1_out), .out(X000), .sel(2'b00));
  Divider #(.width(14)) divider_2 (.a(register_1_q), .b(14'h3e8), .rem(divider_2_rem));  // open: out, upper
  Divider #(.width(14)) divider_3 (.a(divider_2_rem), .b(14'h64), .out(divider_3_out));  // open: upper, rem
  Divider #(.width(14)) divider_4 (.a(register_1_q), .b(14'h64), .rem(divider_4_rem));  // open: out, upper
  Divider #(.width(14)) divider_5 (.a(divider_4_rem), .b(14'ha), .out(divider_5_out));  // open: upper, rem
  BitSelector #(.width(14), .group(4)) bitselector_2 (.in(divider_3_out), .out(_0X00), .sel(2'b00));
  Divider #(.width(14)) divider_6 (.a(register_1_q), .b(14'ha), .rem(divider_6_rem));  // open: out, upper
  BitSelector #(.width(14), .group(4)) bitselector_3 (.in(divider_5_out), .out(_00X0), .sel(2'b00));
  BitSelector #(.width(14), .group(4)) bitselector_4 (.in(divider_6_rem), .out(_000X), .sel(2'b00));
endmodule
