// Logisim project SkinMemo.circ as structural Verilog: 1 circuit, main circuit main
module main (
  input  [1:0] in_1,
  input  in_2,
  input  in_3
);

  wire [7:0] and_1_out, and_2_out, bit_extender_1_out, bit_extender_2_out, or_1_out, rom_1_data, rom_2_data;

  ROM #(.addrWidth(2)) rom_1 (.addr(in_1), .data(rom_1_data));  // open: sel
  assign bit_extender_1_out = {{7{in_2}}, in_2};  // Bit_Extender bit_extender_1
  ROM #(.addrWidth(2)) rom_2 (.addr(in_1), .data(rom_2_data));  // open: sel
  assign bit_extender_2_out = {{7{in_3}}, in_3};  // Bit_Extender bit_extender_2
  assign and_1_out = rom_1_data & bit_extender_1_out;  // AND_Gate and_1, 8 bits wide
  assign and_2_out = rom_2_data & bit_extender_2_out;  // AND_Gate and_2, 8 bits wide
  // Probe on or_1_out
  assign or_1_out = and_1_out | and_2_out;  // OR_Gate or_1, 8 bits wide

  // Notes on the sheet:
  //   contents of rom_1 (hex, n*v repeats v):
  //   1 2 3 4
  //   contents of rom_2 (hex, n*v repeats v):
  //   1a 2b 3c 4d
endmodule
