// Logisim project Sterowanie-timber-ekran-na-2ROM.circ as structural Verilog: 1 circuit, main circuit main
module main (
);

  wire and_1_out, clock_1_out, or_1_out;
  wire [1:0] comparator_1_eq, register_1_q;
  wire [6:0] keyboard_1_data;
  wire [31:0] or_2_out, rom_1_data, rom_2_data;

  Clock clock_1 (.out(clock_1_out));
  Keyboard keyboard_1 (.clk(clock_1_out), .data(keyboard_1_data));  // open: re, clr, avail
  Comparator #(.width(7)) comparator_1 (.a(keyboard_1_data), .b(7'b1100001), .eq(comparator_1_eq[0]));  // open: gt, lt
  Comparator #(.width(7)) comparator_2 (.a(keyboard_1_data), .b(7'b1100100), .eq(comparator_1_eq[1]));  // open: gt, lt
  or or_1 (or_1_out, comparator_1_eq[1], comparator_1_eq[0]);
  Register #(.width(2)) register_1 (.D(comparator_1_eq), .Q(register_1_q), .clk(and_1_out));  // open: en, clr
  and and_1 (and_1_out, or_1_out, clock_1_out);
  ROM #(.addrWidth(2), .dataWidth(32)) rom_1 (.addr(register_1_q), .data(rom_1_data));  // open: sel
  ROM #(.addrWidth(2), .dataWidth(32)) rom_2 (.addr(register_1_q), .data(rom_2_data));  // open: sel
  assign or_2_out = rom_1_data | rom_2_data;  // OR_Gate or_2, 32 bits wide
  DotMatrix #(.inputtype("row"), .matrixrows(6)) dotmatrix_1 (
    .row0(or_2_out[4:0]), .row1(or_2_out[9:5]), .row2(or_2_out[14:10]), .row3(or_2_out[19:15]),
    .row4(or_2_out[24:20]), .row5(or_2_out[29:25]));

  // Notes on the sheet:
  //   contents of rom_1 (hex, n*v repeats v):
  //   0 8421084 8421084
  //   contents of rom_2 (hex, n*v repeats v):
  //   0 21000000 2100000
endmodule
