// Logisim project Stop-countera.circ as structural Verilog: 1 circuit, main circuit main
module main (
  input  CLK,
  input  Reset,
  input  [4:0] Number_of_tics,
  output Tics_out
);

  wire comparator_1_eq, comparator_1_gt, d_ff_1_q, d_ff_2_q;
  wire [4:0] counter_1_q;

  or or_1 (Tics_out, d_ff_2_q, CLK);
  Counter #(.width(5), .max('h1f)) counter_1 (
    .Q(counter_1_q), .clk(Tics_out), .clr(comparator_1_gt));  // open: load, D, count, carry
  Comparator #(.width(5), .mode("unsigned")) comparator_1 (
    .a(counter_1_q), .b(Number_of_tics), .gt(comparator_1_gt), .eq(comparator_1_eq));  // open: lt
  D_Flip_Flop d_ff_1 (.clk(Tics_out), .D(comparator_1_eq), .Q(d_ff_1_q), .reset(Reset));  // open: Qn, preset, en
  D_Flip_Flop d_ff_2 (.Q(d_ff_2_q), .preset(d_ff_1_q), .reset(Reset));  // open: clk, D, Qn, en
endmodule
