// Logisim project Stop_countera.circ as structural Verilog: 1 circuit, main circuit main
module main (
  input  Clk,
  input  Reset,
  output [2:0] Counter
);

  wire counter_1_carry, d_ff_1_q, d_ff_2_q, or_1_out;

  or or_1 (or_1_out, d_ff_2_q, Clk);
  Counter #(.width(3), .max('h7)) counter_1 (
    .Q(Counter), .carry(counter_1_carry), .clk(or_1_out));  // open: load, D, count, clr
  D_Flip_Flop d_ff_1 (.clk(or_1_out), .D(counter_1_carry), .Q(d_ff_1_q), .reset(Reset));  // open: Qn, preset, en
  D_Flip_Flop d_ff_2 (.Q(d_ff_2_q), .preset(d_ff_1_q), .reset(Reset));  // open: clk, D, Qn, en
endmodule
