// Logisim project TIMEDISPLAY.circ as structural Verilog: 1 circuit, main circuit main
module main (
  input  WHEN_1__SUB_TIME_ONE_TICK__WHEN_0_ADD_TIME_ON_TICK,
  input  CLK,
  input  RESET,
  output TIME_OUT,
  output [31:0] OutputScreen
);

  wire not_1_out, shift_register_1_q0, shift_register_1_q1, shift_register_1_q2, shift_register_1_q3,
       shift_register_1_q4, shift_register_1_q5, shift_register_1_q6, shift_register_1_q7,
       shift_register_1_q8, shift_register_1_q9, shift_register_1_q10, shift_register_1_q11,
       shift_register_1_q12, shift_register_1_q13, shift_register_1_q14, shift_register_1_q15,
       shift_register_1_q16, shift_register_1_q17, shift_register_1_q18, shift_register_1_q19,
       shift_register_1_q20, shift_register_1_q21, shift_register_1_q22, shift_register_1_q23,
       shift_register_1_q24, shift_register_1_q25, shift_register_1_q26, shift_register_1_q27,
       shift_register_1_q28, shift_register_1_q29, shift_register_1_q30, shift_register_1_q31;

  not not_1 (not_1_out, WHEN_1__SUB_TIME_ONE_TICK__WHEN_0_ADD_TIME_ON_TICK);
  Shift_Register #(.length(32)) shift_register_1 (
    .shift(WHEN_1__SUB_TIME_ONE_TICK__WHEN_0_ADD_TIME_ON_TICK), .in(1'b1), .clk(CLK), .out(TIME_OUT),
    .load(not_1_out), .clr(RESET), .d0(shift_register_1_q1), .q0(shift_register_1_q0),
    .d1(shift_register_1_q2), .q1(shift_register_1_q1), .d2(shift_register_1_q3), .q2(shift_register_1_q2),
    .d3(shift_register_1_q4), .q3(shift_register_1_q3), .d4(shift_register_1_q5), .q4(shift_register_1_q4),
    .d5(shift_register_1_q6), .q5(shift_register_1_q5), .d6(shift_register_1_q7), .q6(shift_register_1_q6),
    .d7(shift_register_1_q8), .q7(shift_register_1_q7), .d8(shift_register_1_q9), .q8(shift_register_1_q8),
    .d9(shift_register_1_q10), .q9(shift_register_1_q9), .d10(shift_register_1_q11),
    .q10(shift_register_1_q10), .d11(shift_register_1_q12), .q11(shift_register_1_q11),
    .d12(shift_register_1_q13), .q12(shift_register_1_q12), .d13(shift_register_1_q14),
    .q13(shift_register_1_q13), .d14(shift_register_1_q15), .q14(shift_register_1_q14),
    .d15(shift_register_1_q16), .q15(shift_register_1_q15), .d16(shift_register_1_q17),
    .q16(shift_register_1_q16), .d17(shift_register_1_q18), .q17(shift_register_1_q17),
    .d18(shift_register_1_q19), .q18(shift_register_1_q18), .d19(shift_register_1_q20),
    .q19(shift_register_1_q19), .d20(shift_register_1_q21), .q20(shift_register_1_q20),
    .d21(shift_register_1_q22), .q21(shift_register_1_q21), .d22(shift_register_1_q23),
    .q22(shift_register_1_q22), .d23(shift_register_1_q24), .q23(shift_register_1_q23),
    .d24(shift_register_1_q25), .q24(shift_register_1_q24), .d25(shift_register_1_q26),
    .q25(shift_register_1_q25), .d26(shift_register_1_q27), .q26(shift_register_1_q26),
    .d27(shift_register_1_q28), .q27(shift_register_1_q27), .d28(shift_register_1_q29),
    .q28(shift_register_1_q28), .d29(shift_register_1_q30), .q29(shift_register_1_q29),
    .d30(shift_register_1_q31), .q30(shift_register_1_q30), .d31(1'b0), .q31(shift_register_1_q31));
  not not_2 (OutputScreen[30], shift_register_1_q1);
  not not_3 (OutputScreen[31], shift_register_1_q0);
  not not_4 (OutputScreen[25], shift_register_1_q6);
  not not_5 (OutputScreen[27], shift_register_1_q4);
  not not_6 (OutputScreen[28], shift_register_1_q3);
  not not_7 (OutputScreen[22], shift_register_1_q9);
  not not_8 (OutputScreen[24], shift_register_1_q7);
  not not_9 (OutputScreen[23], shift_register_1_q8);
  not not_10 (OutputScreen[29], shift_register_1_q2);
  not not_11 (OutputScreen[26], shift_register_1_q5);
  not not_12 (OutputScreen[16], shift_register_1_q15);
  not not_13 (OutputScreen[20], shift_register_1_q11);
  not not_14 (OutputScreen[15], shift_register_1_q16);
  not not_15 (OutputScreen[19], shift_register_1_q12);
  not not_16 (OutputScreen[14], shift_register_1_q17);
  not not_17 (OutputScreen[21], shift_register_1_q10);
  not not_18 (OutputScreen[17], shift_register_1_q14);
  not not_19 (OutputScreen[18], shift_register_1_q13);
  not not_20 (OutputScreen[13], shift_register_1_q18);
  not not_21 (OutputScreen[10], shift_register_1_q21);
  not not_22 (OutputScreen[7], shift_register_1_q24);
  not not_23 (OutputScreen[12], shift_register_1_q19);
  not not_24 (OutputScreen[11], shift_register_1_q20);
  not not_25 (OutputScreen[8], shift_register_1_q23);
  not not_26 (OutputScreen[6], shift_register_1_q25);
  not not_27 (OutputScreen[9], shift_register_1_q22);
  not not_28 (OutputScreen[5], shift_register_1_q26);
  not not_29 (OutputScreen[0], shift_register_1_q31);
  not not_30 (OutputScreen[4], shift_register_1_q27);
  not not_31 (OutputScreen[2], shift_register_1_q29);
  not not_32 (OutputScreen[3], shift_register_1_q28);
  not not_33 (OutputScreen[1], shift_register_1_q30);
endmodule
