// Logisim project Timer.circ as structural Verilog: 1 circuit, main circuit main
module main (
  input  in_1,
  input  in_2,
  input  in_3,
  output END_GAME
);

  wire [31:0] main_1_outputscreen;

  TIMEDISPLAY_main main_1 (
    .WHEN_1__SUB_TIME_ONE_TICK__WHEN_0_ADD_TIME_ON_TICK(in_1), .CLK(in_3), .RESET(in_2),
    .OutputScreen(main_1_outputscreen), .TIME_OUT(END_GAME));
  DotMatrix #(.matrixcols(32), .matrixrows(1)) dotmatrix_1 (
    .col0(main_1_outputscreen[31]), .col1(main_1_outputscreen[30]), .col2(main_1_outputscreen[29]),
    .col3(main_1_outputscreen[28]), .col4(main_1_outputscreen[27]), .col5(main_1_outputscreen[26]),
    .col6(main_1_outputscreen[25]), .col7(main_1_outputscreen[24]), .col8(main_1_outputscreen[23]),
    .col9(main_1_outputscreen[22]), .col10(main_1_outputscreen[21]), .col11(main_1_outputscreen[20]),
    .col12(main_1_outputscreen[19]), .col13(main_1_outputscreen[18]), .col14(main_1_outputscreen[17]),
    .col15(main_1_outputscreen[16]), .col16(main_1_outputscreen[15]), .col17(main_1_outputscreen[14]),
    .col18(main_1_outputscreen[13]), .col19(main_1_outputscreen[12]), .col20(main_1_outputscreen[11]),
    .col21(main_1_outputscreen[10]), .col22(main_1_outputscreen[9]), .col23(main_1_outputscreen[8]),
    .col24(main_1_outputscreen[7]), .col25(main_1_outputscreen[6]), .col26(main_1_outputscreen[5]),
    .col27(main_1_outputscreen[4]), .col28(main_1_outputscreen[3]), .col29(main_1_outputscreen[2]),
    .col30(main_1_outputscreen[1]), .col31(main_1_outputscreen[0]));
endmodule
