// Logisim project 24_bit_register.circ as structural Verilog: 1 circuit, main circuit main
module main (
  input  [23:0] Input,
  input  CLK,
  input  Reset,
  output [23:0] Output
);

  D_Flip_Flop d_ff_1 (.clk(CLK), .D(Input[0]), .Q(Output[0]), .reset(Reset));  // open: Qn, preset, en
  D_Flip_Flop d_ff_2 (.clk(CLK), .D(Input[1]), .Q(Output[1]), .reset(Reset));  // open: Qn, preset, en
  D_Flip_Flop d_ff_3 (.clk(CLK), .D(Input[2]), .Q(Output[2]), .reset(Reset));  // open: Qn, preset, en
  D_Flip_Flop d_ff_4 (.clk(CLK), .D(Input[3]), .Q(Output[3]), .reset(Reset));  // open: Qn, preset, en
  D_Flip_Flop d_ff_5 (.clk(CLK), .D(Input[4]), .Q(Output[4]), .reset(Reset));  // open: Qn, preset, en
  D_Flip_Flop d_ff_6 (.clk(CLK), .D(Input[5]), .Q(Output[5]), .reset(Reset));  // open: Qn, preset, en
  D_Flip_Flop d_ff_7 (.clk(CLK), .D(Input[6]), .Q(Output[6]), .reset(Reset));  // open: Qn, preset, en
  D_Flip_Flop d_ff_8 (.clk(CLK), .D(Input[7]), .Q(Output[7]), .reset(Reset));  // open: Qn, preset, en
  D_Flip_Flop d_ff_9 (.clk(CLK), .D(Input[8]), .Q(Output[8]), .reset(Reset));  // open: Qn, preset, en
  D_Flip_Flop d_ff_10 (.clk(CLK), .D(Input[9]), .Q(Output[9]), .reset(Reset));  // open: Qn, preset, en
  D_Flip_Flop d_ff_11 (.clk(CLK), .D(Input[10]), .Q(Output[10]), .reset(Reset));  // open: Qn, preset, en
  D_Flip_Flop d_ff_12 (.clk(CLK), .D(Input[11]), .Q(Output[11]), .reset(Reset));  // open: Qn, preset, en
  D_Flip_Flop d_ff_13 (.clk(CLK), .D(Input[12]), .Q(Output[12]), .reset(Reset));  // open: Qn, preset, en
  D_Flip_Flop d_ff_14 (.clk(CLK), .D(Input[13]), .Q(Output[13]), .reset(Reset));  // open: Qn, preset, en
  D_Flip_Flop d_ff_15 (.clk(CLK), .D(Input[14]), .Q(Output[14]), .reset(Reset));  // open: Qn, preset, en
  D_Flip_Flop d_ff_16 (.clk(CLK), .D(Input[15]), .Q(Output[15]), .reset(Reset));  // open: Qn, preset, en
  D_Flip_Flop d_ff_17 (.clk(CLK), .D(Input[16]), .Q(Output[16]), .reset(Reset));  // open: Qn, preset, en
  D_Flip_Flop d_ff_18 (.clk(CLK), .D(Input[17]), .Q(Output[17]), .reset(Reset));  // open: Qn, preset, en
  D_Flip_Flop d_ff_19 (.clk(CLK), .D(Input[18]), .Q(Output[18]), .reset(Reset));  // open: Qn, preset, en
  D_Flip_Flop d_ff_20 (.clk(CLK), .D(Input[19]), .Q(Output[19]), .reset(Reset));  // open: Qn, preset, en
  D_Flip_Flop d_ff_21 (.clk(CLK), .D(Input[20]), .Q(Output[20]), .reset(Reset));  // open: Qn, preset, en
  D_Flip_Flop d_ff_22 (.clk(CLK), .D(Input[21]), .Q(Output[21]), .reset(Reset));  // open: Qn, preset, en
  D_Flip_Flop d_ff_23 (.clk(CLK), .D(Input[22]), .Q(Output[22]), .reset(Reset));  // open: Qn, preset, en
  D_Flip_Flop d_ff_24 (.clk(CLK), .D(Input[23]), .Q(Output[23]), .reset(Reset));  // open: Qn, preset, en
endmodule
