// Logisim project 4_bit_counter.circ as structural Verilog: 1 circuit, main circuit main
module main (
  input  CLK,
  input  RESET,
  output [3:0] Hex,
  output Next
);

  wire d_ff_1_qn, d_ff_2_qn, d_ff_3_qn, d_ff_4_qn, or_1_out, or_2_out, or_3_out, or_4_out;

  D_Flip_Flop d_ff_1 (.clk(CLK), .D(d_ff_1_qn), .Q(Hex[0]), .Qn(d_ff_1_qn), .reset(or_1_out));  // open: preset, en
  or or_1 (or_1_out, RESET, Next);
  D_Flip_Flop d_ff_2 (
    .clk(d_ff_1_qn), .D(d_ff_2_qn), .Q(Hex[1]), .Qn(d_ff_2_qn), .reset(or_2_out));  // open: preset, en
  or or_2 (or_2_out, RESET, Next);
  D_Flip_Flop d_ff_3 (
    .clk(d_ff_2_qn), .D(d_ff_3_qn), .Q(Hex[2]), .Qn(d_ff_3_qn), .reset(or_3_out));  // open: preset, en
  or or_3 (or_3_out, RESET, Next);
  D_Flip_Flop d_ff_4 (
    .clk(d_ff_3_qn), .D(d_ff_4_qn), .Q(Hex[3]), .Qn(d_ff_4_qn), .reset(or_4_out));  // open: preset, en
  or or_4 (or_4_out, RESET, Next);
  and and_1 (Next, Hex[1], Hex[3]);
endmodule
