// Logisim project 8x24_register.circ as structural Verilog: 1 circuit, main circuit main
module main (
  input  [23:0] in_1,
  input  [23:0] in_2,
  input  [23:0] in_3,
  input  [23:0] in_4,
  input  [23:0] in_5,
  input  [23:0] in_6,
  input  [23:0] in_7,
  input  [23:0] in_8,
  input  Clock,
  input  Reset,
  output [23:0] out_11,
  output [23:0] out_12,
  output [23:0] out_13,
  output [23:0] out_14,
  output [23:0] out_15,
  output [23:0] out_16,
  output [23:0] out_17,
  output [23:0] out_18
);

  _24_bit_register_main main_1 (.Input(in_1), .Output(out_11), .CLK(Clock), .Reset(Reset));
  _24_bit_register_main main_2 (.Input(in_2), .Output(out_12), .CLK(Clock), .Reset(Reset));
  _24_bit_register_main main_3 (.Input(in_3), .Output(out_13), .CLK(Clock), .Reset(Reset));
  _24_bit_register_main main_4 (.Input(in_4), .Output(out_14), .CLK(Clock), .Reset(Reset));
  _24_bit_register_main main_5 (.Input(in_5), .Output(out_15), .CLK(Clock), .Reset(Reset));
  _24_bit_register_main main_6 (.Input(in_6), .Output(out_16), .CLK(Clock), .Reset(Reset));
  _24_bit_register_main main_7 (.Input(in_7), .Output(out_17), .CLK(Clock), .Reset(Reset));
  _24_bit_register_main main_8 (.Input(in_8), .Output(out_18), .CLK(Clock), .Reset(Reset));
endmodule
