// Logisim project 8x24_register_address.circ as structural Verilog: 1 circuit, main circuit main
module main (
  input  [23:0] in_1,
  input  [23:0] in_2,
  input  [23:0] in_3,
  input  [23:0] in_4,
  input  [23:0] in_5,
  input  [23:0] in_6,
  input  [23:0] in_7,
  input  [23:0] in_8,
  input  Reset,
  input  Clock,
  input  [2:0] Address,
  output [23:0] out_12,
  output [23:0] out_13,
  output [23:0] out_14,
  output [23:0] out_15,
  output [23:0] out_16,
  output [23:0] out_17,
  output [23:0] out_18,
  output [23:0] out_19
);

  wire demultiplexer_1_out0, demultiplexer_1_out1, demultiplexer_1_out2, demultiplexer_1_out3,
       demultiplexer_1_out4, demultiplexer_1_out5, demultiplexer_1_out6, demultiplexer_1_out7;

  Demultiplexer #(.select(3)) demultiplexer_1 (
    .out0(demultiplexer_1_out0), .out1(demultiplexer_1_out1), .out2(demultiplexer_1_out2),
    .out3(demultiplexer_1_out3), .out4(demultiplexer_1_out4), .out5(demultiplexer_1_out5),
    .out6(demultiplexer_1_out6), .out7(demultiplexer_1_out7), .in(Clock), .sel(Address));  // open: en
  _24_bit_register_main main_1 (.Input(in_1), .Output(out_12), .CLK(demultiplexer_1_out0), .Reset(Reset));
  _24_bit_register_main main_2 (.Input(in_2), .Output(out_13), .CLK(demultiplexer_1_out1), .Reset(Reset));
  _24_bit_register_main main_3 (.Input(in_3), .Output(out_14), .CLK(demultiplexer_1_out2), .Reset(Reset));
  _24_bit_register_main main_4 (.Input(in_4), .Output(out_15), .CLK(demultiplexer_1_out3), .Reset(Reset));
  _24_bit_register_main main_5 (.Input(in_5), .Output(out_16), .CLK(demultiplexer_1_out4), .Reset(Reset));
  _24_bit_register_main main_6 (.Input(in_6), .Output(out_17), .CLK(demultiplexer_1_out5), .Reset(Reset));
  _24_bit_register_main main_7 (.Input(in_7), .Output(out_18), .CLK(demultiplexer_1_out6), .Reset(Reset));
  _24_bit_register_main main_8 (.Input(in_8), .Output(out_19), .CLK(demultiplexer_1_out7), .Reset(Reset));
endmodule
