// Logisim project 9999_counter.circ as structural Verilog: 1 circuit, main circuit main
module main (
  input  CLK,
  input  RESET,
  output [3:0] out_3,
  output [3:0] out_4,
  output [3:0] out_5,
  output [3:0] out_6
);

  wire main_1_next, main_2_next, main_3_next;

  _4_bit_counter_main main_1 (.Hex(out_3), .CLK(CLK), .RESET(RESET), .Next(main_1_next));
  _4_bit_counter_main main_2 (.Hex(out_4), .CLK(main_1_next), .RESET(RESET), .Next(main_2_next));
  _4_bit_counter_main main_3 (.Hex(out_5), .CLK(main_2_next), .RESET(RESET), .Next(main_3_next));
  _4_bit_counter_main main_4 (.Hex(out_6), .CLK(main_3_next), .RESET(RESET));  // open: Next
endmodule
