// Logisim project Counter_resetting_circuit.circ as structural Verilog: 1 circuit, main circuit main
module main (
  input  [1:0] Keyboard_value,
  input  Clk,
  output Out
);

  wire comparator_1_eq, comparator_2_eq, or_1_out;
  wire [1:0] register_1_q, register_2_q;

  Register #(.width(2)) register_1 (.D(Keyboard_value), .Q(register_1_q), .clk(Clk));  // open: en, clr
  Comparator #(.width(2)) comparator_1 (.a(Keyboard_value), .b(2'b10), .eq(comparator_1_eq));  // open: gt, lt
  Comparator #(.width(2)) comparator_2 (.a(Keyboard_value), .b(2'b01), .eq(comparator_2_eq));  // open: gt, lt
  Register #(.width(2)) register_2 (.D(register_1_q), .Q(register_2_q), .clk(or_1_out));  // open: en, clr
  or or_1 (or_1_out, comparator_1_eq, comparator_2_eq);
  Comparator #(.width(2)) comparator_3 (.a(Keyboard_value), .b(register_2_q), .eq(Out));  // open: gt, lt
endmodule
