// Logisim project Display_first_segment_control.circ as structural Verilog: 1 circuit, main circuit main
module main (
  input  [23:0] In,
  input  Clk,
  input  Reset,
  input  [2:0] Counter,
  output [23:0] O1,
  output [23:0] O2,
  output [23:0] O2_2,
  output [23:0] O2_3,
  output [23:0] O2_4,
  output [23:0] O2_5,
  output [23:0] O2_6,
  output [23:0] O2_7
);

  wire comparator_1_eq;
  wire [23:0] demultiplexer_1_out0, demultiplexer_1_out1, demultiplexer_1_out2, demultiplexer_1_out3,
       demultiplexer_1_out4, demultiplexer_1_out5, demultiplexer_1_out6, demultiplexer_1_out7, main_1_out_12,
       main_1_out_13, main_1_out_14, main_1_out_15, main_1_out_16, main_1_out_17, main_1_out_18,
       main_1_out_19;

  Demultiplexer #(.select(3), .width(24)) demultiplexer_1 (
    .out0(demultiplexer_1_out0), .out1(demultiplexer_1_out1), .out2(demultiplexer_1_out2),
    .out3(demultiplexer_1_out3), .out4(demultiplexer_1_out4), .out5(demultiplexer_1_out5),
    .out6(demultiplexer_1_out6), .out7(demultiplexer_1_out7), .in(In), .sel(Counter));  // open: en
  _8x24_register_address_main main_1 (
    .in_1(demultiplexer_1_out0), .in_2(demultiplexer_1_out1), .in_3(demultiplexer_1_out2),
    .in_4(demultiplexer_1_out3), .in_5(demultiplexer_1_out4), .in_6(demultiplexer_1_out5),
    .in_7(demultiplexer_1_out6), .in_8(demultiplexer_1_out7), .out_12(main_1_out_12), .out_13(main_1_out_13),
    .out_14(main_1_out_14), .out_15(main_1_out_15), .out_16(main_1_out_16), .out_17(main_1_out_17),
    .out_18(main_1_out_18), .out_19(main_1_out_19), .Reset(Reset), .Address(Counter), .Clock(Clk));
  _8x24_register_main main_2 (
    .in_1(main_1_out_12), .in_2(main_1_out_13), .in_3(main_1_out_14), .in_4(main_1_out_15),
    .in_5(main_1_out_16), .in_6(main_1_out_17), .in_7(main_1_out_18), .in_8(main_1_out_19), .out_11(O1),
    .out_12(O2), .out_13(O2_2), .out_14(O2_3), .out_15(O2_4), .out_16(O2_5), .out_17(O2_6), .out_18(O2_7),
    .Clock(comparator_1_eq), .Reset(Reset));
  Comparator #(.width(3)) comparator_1 (.a(Counter), .b(3'b000), .eq(comparator_1_eq));  // open: gt, lt
endmodule
