// Logisim project Display_segment_control.circ as structural Verilog: 1 circuit, main circuit main
module main (
  input  [23:0] ROM_in,
  input  Reset,
  input  Clk,
  output [23:0] out_4,
  output [23:0] out_5,
  output [23:0] out_6,
  output [23:0] out_7,
  output [23:0] out_8,
  output [23:0] out_9,
  output [23:0] out_10,
  output [23:0] out_11
);

  wire comparator_1_eq, comparator_2_eq, controlled_buffer_1_out;
  wire [2:0] counter_1_q;
  wire [23:0] and_1_out, demultiplexer_1_out0, demultiplexer_1_out1, demultiplexer_1_out2,
       demultiplexer_1_out3, demultiplexer_1_out4, demultiplexer_1_out5, demultiplexer_1_out6,
       demultiplexer_1_out7, main_1_out_12, main_1_out_13, main_1_out_14, main_1_out_15, main_1_out_16,
       main_1_out_17, main_1_out_18, main_1_out_19;

  assign controlled_buffer_1_out = comparator_2_eq ? Clk : 1'bz;  // Controlled_Buffer controlled_buffer_1
  Demultiplexer #(.select(3), .width(24)) demultiplexer_1 (
    .out0(demultiplexer_1_out0), .out1(demultiplexer_1_out1), .out2(demultiplexer_1_out2),
    .out3(demultiplexer_1_out3), .out4(demultiplexer_1_out4), .out5(demultiplexer_1_out5),
    .out6(demultiplexer_1_out6), .out7(demultiplexer_1_out7), .in(ROM_in), .sel(counter_1_q));  // open: en
  Counter #(.width(3), .max('h7)) counter_1 (
    .Q(counter_1_q), .clk(controlled_buffer_1_out));  // open: load, D, count, carry, clr
  _8x24_register_address_main main_1 (
    .in_1(demultiplexer_1_out0), .in_2(demultiplexer_1_out1), .in_3(demultiplexer_1_out2),
    .in_4(demultiplexer_1_out3), .in_5(demultiplexer_1_out4), .in_6(demultiplexer_1_out5),
    .in_7(demultiplexer_1_out6), .in_8(demultiplexer_1_out7), .out_12(main_1_out_12), .out_13(main_1_out_13),
    .out_14(main_1_out_14), .out_15(main_1_out_15), .out_16(main_1_out_16), .out_17(main_1_out_17),
    .out_18(main_1_out_18), .out_19(main_1_out_19), .Reset(Reset), .Address(counter_1_q),
    .Clock(controlled_buffer_1_out));
  _8x24_register_main main_2 (
    .in_1(main_1_out_12), .in_2(main_1_out_13), .in_3(main_1_out_14), .in_4(main_1_out_15),
    .in_5(main_1_out_16), .in_6(main_1_out_17), .in_7(main_1_out_18), .in_8(main_1_out_19), .out_11(out_4),
    .out_12(out_5), .out_13(out_6), .out_14(out_7), .out_15(out_8), .out_16(out_9), .out_17(out_10),
    .out_18(out_11), .Clock(comparator_1_eq), .Reset(Reset));
  Comparator #(.width(3)) comparator_1 (.a(counter_1_q), .b(3'b000), .eq(comparator_1_eq));  // open: gt, lt
  assign and_1_out = out_4 & out_11;  // AND_Gate and_1, 24 bits wide
  Comparator #(.width(24)) comparator_2 (.a(and_1_out), .b({24{1'b0}}), .eq(comparator_2_eq));  // open: gt, lt
endmodule
