// Logisim project Dynamic_difficulty_control.circ as structural Verilog: 1 circuit, main circuit main
module main (
  input  [13:0] Points_value,
  input  Stop,
  output Clk_timebar
);

  wire and_1_out, and_2_out, comparator_1_gt, comparator_1_lt, comparator_2_gt, Easy_out, Hard_out,
       Medium_out, multiplexer_1_out, not_1_out, not_2_out;

  Comparator #(.width(14)) comparator_1 (
    .a(Points_value), .b(14'h32), .gt(comparator_1_gt), .lt(comparator_1_lt));  // open: eq
  Comparator #(.width(14)) comparator_2 (.a(Points_value), .b(14'h64), .gt(comparator_2_gt));  // open: eq, lt
  Clock #(.highDuration(40), .lowDuration(30)) Easy (.out(Easy_out));
  Clock #(.highDuration(20), .lowDuration(20)) Medium (.out(Medium_out));
  Clock #(.highDuration(10), .lowDuration(10)) Hard (.out(Hard_out));
  and and_1 (and_1_out, comparator_1_gt, comparator_2_gt);
  Multiplexer multiplexer_1 (
    .in0(Medium_out), .in1(Hard_out), .out(multiplexer_1_out), .sel(and_1_out), .en(not_2_out));
  buf and_2 (and_2_out, not_1_out);  // AND_Gate
  not not_1 (not_1_out, comparator_1_lt);
  not not_2 (not_2_out, Stop);
  Multiplexer multiplexer_2 (
    .in0(Easy_out), .in1(multiplexer_1_out), .out(Clk_timebar), .sel(and_2_out), .en(not_2_out));
endmodule
