// Logisim project Key_recognition.circ as structural Verilog: 1 circuit, main circuit main
module main (
  input  [6:0] Keyboard_input,
  input  Clk,
  output A,
  output [1:0] Out,
  output KeyImpulse,
  output D
);

  wire and_1_out, comparator_1_eq, comparator_2_eq, comparator_3_eq, comparator_4_eq;
  wire [1:0] or_2_out;

  Comparator #(.width(7)) comparator_1 (.a(Keyboard_input), .b(7'b1100001), .eq(comparator_1_eq));  // open: gt, lt
  Comparator #(.width(7)) comparator_2 (.a(Keyboard_input), .b(7'b1000001), .eq(comparator_2_eq));  // open: gt, lt
  Comparator #(.width(7)) comparator_3 (.a(Keyboard_input), .b(7'b1100100), .eq(comparator_3_eq));  // open: gt, lt
  Comparator #(.width(7)) comparator_4 (.a(Keyboard_input), .b(7'b1000100), .eq(comparator_4_eq));  // open: gt, lt
  or or_1 (or_2_out[1], comparator_1_eq, comparator_2_eq);
  or or_2 (or_2_out[0], comparator_3_eq, comparator_4_eq);
  or or_3 (KeyImpulse, or_2_out[0], or_2_out[1]);
  and and_1 (and_1_out, KeyImpulse, Clk);
  Register #(.width(2)) register_1 (.D(or_2_out), .Q(Out), .clk(and_1_out));  // open: en, clr
  Register #(.width(1)) register_2 (.D(or_2_out[1]), .Q(A), .clk(or_2_out[1]), .clr(or_2_out[0]));  // open: en
  Register #(.width(1)) register_3 (.D(or_2_out[0]), .Q(D), .clk(or_2_out[0]), .clr(or_2_out[1]));  // open: en

  // Notes on the sheet:
  //   A key
  //   D key
  //   Space
endmodule
