// Logisim project Over_screen.circ as structural Verilog: 1 circuit, main circuit main
module main (
  input  [23:0] Input,
  input  Animation_Clock,
  input  Key_impulse,
  input  Reset__tree,
  input  in_5,
  output Clk_out,
  output [23:0] Reg_out,
  output [23:0] Out_0,
  output [23:0] Out_1,
  output [23:0] Out_2,
  output [23:0] Out_3,
  output [23:0] Out_4,
  output [23:0] Out_5,
  output [23:0] Out_6,
  output [23:0] Out_7
);

  wire [23:0] controlled_buffer_1_out, controlled_buffer_2_out, controlled_buffer_3_out,
       controlled_buffer_4_out, controlled_buffer_5_out, controlled_buffer_6_out, controlled_buffer_7_out,
       controlled_buffer_8_out, main_1_o0, main_1_o1, main_1_o2, main_1_o3, main_1_o4, main_1_o5, main_1_o6,
       main_1_o7, rom_1_data, rom_2_data, rom_3_data, rom_4_data, rom_5_data, rom_6_data, rom_7_data,
       rom_8_data;

  Screen_animation_segment_main main_1 (
    .Input_line(Input), .Impulse(Key_impulse), .Reset(Reset__tree), .O0(main_1_o0), .O1(main_1_o1),
    .O2(main_1_o2), .Register_out(Reg_out), .O3(main_1_o3), .O4(main_1_o4), .O5(main_1_o5), .O6(main_1_o6),
    .O7(main_1_o7), .Clk_out(Clk_out), .Clk(Animation_Clock));
  ROM #(.addrWidth(2), .dataWidth(24)) rom_1 (.addr(2'b00), .data(rom_1_data));  // open: sel
  ROM #(.addrWidth(2), .dataWidth(24)) rom_2 (.addr(2'b00), .data(rom_2_data));  // open: sel
  ROM #(.addrWidth(2), .dataWidth(24)) rom_3 (.addr(2'b00), .data(rom_3_data));  // open: sel
  ROM #(.addrWidth(2), .dataWidth(24)) rom_4 (.addr(2'b00), .data(rom_4_data));  // open: sel
  ROM #(.addrWidth(2), .dataWidth(24)) rom_5 (.addr(2'b00), .data(rom_5_data));  // open: sel
  ROM #(.addrWidth(2), .dataWidth(24)) rom_6 (.addr(2'b00), .data(rom_6_data));  // open: sel
  ROM #(.addrWidth(2), .dataWidth(24)) rom_7 (.addr(2'b00), .data(rom_7_data));  // open: sel
  ROM #(.addrWidth(2), .dataWidth(24)) rom_8 (.addr(2'b00), .data(rom_8_data));  // open: sel
  assign controlled_buffer_1_out = in_5 ? rom_1_data : 24'bz;  // Controlled_Buffer controlled_buffer_1
  Pull_Resistor pull_resistor_1 (.node(controlled_buffer_1_out));
  assign controlled_buffer_2_out = in_5 ? rom_2_data : 24'bz;  // Controlled_Buffer controlled_buffer_2
  Pull_Resistor pull_resistor_2 (.node(controlled_buffer_2_out));
  assign controlled_buffer_3_out = in_5 ? rom_3_data : 24'bz;  // Controlled_Buffer controlled_buffer_3
  Pull_Resistor pull_resistor_3 (.node(controlled_buffer_3_out));
  assign controlled_buffer_4_out = in_5 ? rom_4_data : 24'bz;  // Controlled_Buffer controlled_buffer_4
  Pull_Resistor pull_resistor_4 (.node(controlled_buffer_4_out));
  assign controlled_buffer_5_out = in_5 ? rom_5_data : 24'bz;  // Controlled_Buffer controlled_buffer_5
  Pull_Resistor pull_resistor_5 (.node(controlled_buffer_5_out));
  assign controlled_buffer_6_out = in_5 ? rom_6_data : 24'bz;  // Controlled_Buffer controlled_buffer_6
  Pull_Resistor pull_resistor_6 (.node(controlled_buffer_6_out));
  assign controlled_buffer_7_out = in_5 ? rom_7_data : 24'bz;  // Controlled_Buffer controlled_buffer_7
  Pull_Resistor pull_resistor_7 (.node(controlled_buffer_7_out));
  assign controlled_buffer_8_out = in_5 ? rom_8_data : 24'bz;  // Controlled_Buffer controlled_buffer_8
  Pull_Resistor pull_resistor_8 (.node(controlled_buffer_8_out));
  assign Out_0 = main_1_o0 | controlled_buffer_1_out;  // OR_Gate or_1, 24 bits wide
  assign Out_1 = main_1_o1 | controlled_buffer_2_out;  // OR_Gate or_2, 24 bits wide
  assign Out_2 = main_1_o2 | controlled_buffer_3_out;  // OR_Gate or_3, 24 bits wide
  assign Out_3 = main_1_o3 | controlled_buffer_4_out;  // OR_Gate or_4, 24 bits wide
  assign Out_4 = main_1_o4 | controlled_buffer_5_out;  // OR_Gate or_5, 24 bits wide
  assign Out_5 = main_1_o5 | controlled_buffer_6_out;  // OR_Gate or_6, 24 bits wide
  assign Out_6 = main_1_o6 | controlled_buffer_7_out;  // OR_Gate or_7, 24 bits wide
  assign Out_7 = main_1_o7 | controlled_buffer_8_out;  // OR_Gate or_8, 24 bits wide

  // Notes on the sheet:
  //   contents of rom_1 (hex, n*v repeats v):
  //   fbec6f
  //   contents of rom_2 (hex, n*v repeats v):
  //   cb6eed
  //   contents of rom_3 (hex, n*v repeats v):
  //   c36fec
  //   contents of rom_4 (hex, n*v repeats v):
  //   dbed6f
  //   contents of rom_5 (hex, n*v repeats v):
  //   cb6c6c
  //   contents of rom_6 (hex, n*v repeats v):
  //   cb6c6c
  //   contents of rom_7 (hex, n*v repeats v):
  //   cb6c6d
  //   contents of rom_8 (hex, n*v repeats v):
  //   fb6c6f
endmodule
