// Logisim project ROM_TIMBER.circ as structural Verilog: 1 circuit, main circuit main
module main (
);

  ROM #(.addrWidth(2), .dataWidth(24)) rom_1 ();  // open: addr, data, sel
  ROM #(.addrWidth(2), .dataWidth(24)) rom_2 ();  // open: addr, data, sel
  ROM #(.addrWidth(2), .dataWidth(24)) rom_3 ();  // open: addr, data, sel
  ROM #(.addrWidth(2), .dataWidth(24)) rom_4 ();  // open: addr, data, sel
  ROM #(.addrWidth(2), .dataWidth(24)) rom_5 ();  // open: addr, data, sel
  ROM #(.addrWidth(2), .dataWidth(24)) rom_6 ();  // open: addr, data, sel
  ROM #(.addrWidth(2), .dataWidth(24)) rom_7 ();  // open: addr, data, sel
  ROM #(.addrWidth(2), .dataWidth(24)) rom_8 ();  // open: addr, data, sel

  // Notes on the sheet:
  //   Timber po lewej stronie -> stan 0
  //   Timber po prawej stronie -> stan 1
endmodule
