// Logisim project ROM_Tree.circ as structural Verilog: 1 circuit, main circuit main
module main (
  input  [2:0] Counter,
  output [23:0] ROM_0,
  output [23:0] ROM_1,
  output [23:0] ROM_2,
  output [23:0] ROM_3,
  output [23:0] ROM_4
);

  ROM #(.addrWidth(3), .dataWidth(24)) u_rom_1 (.addr(Counter), .data(ROM_0));  // open: sel
  ROM #(.addrWidth(3), .dataWidth(24)) u_rom_2 (.addr(Counter), .data(ROM_1));  // open: sel
  ROM #(.addrWidth(3), .dataWidth(24)) u_rom_3 (.addr(Counter), .data(ROM_2));  // open: sel
  ROM #(.addrWidth(3), .dataWidth(24)) u_rom_4 (.addr(Counter), .data(ROM_3));  // open: sel
  ROM #(.addrWidth(3), .dataWidth(24)) rom_5 (.addr(Counter), .data(ROM_4));  // open: sel

  // Notes on the sheet:
  //   contents of rom_1 (hex, n*v repeats v):
  //   8*7e00
  //   contents of rom_2 (hex, n*v repeats v):
  //   7e00 7e08 7f1c 7ffe 7f9c 7e08 7e00 7e00
  //   contents of rom_3 (hex, n*v repeats v):
  //   7e00 10fe00 38fe00 7ffe00 39fe00 107e00 7e00 7e00
  //   contents of rom_4 (hex, n*v repeats v):
  //   fb6c6f cb6c6d cb6c6c cb6c6c dbed6f c36fec cb6eed fbec6f
  //   contents of rom_5 (hex, n*v repeats v):
  //   f88fb6 d9cdb6 db6c36 db6c36 db6f3c db6c36 db6db6 fb6fbe
endmodule
