// Logisim project Screen_animation_segment.circ as structural Verilog: 1 circuit, main circuit main
module main (
  input  Clk,
  input  [23:0] Input_line,
  input  Impulse,
  input  Reset,
  output Clk_out,
  output [23:0] O0,
  output [23:0] O1,
  output [23:0] O2,
  output [23:0] Register_out,
  output [23:0] O3,
  output [23:0] O4,
  output [23:0] O5,
  output [23:0] O6,
  output [23:0] O7
);

  wire main_1_tics_out;

  Stop_countera_main main_1 (.CLK(Clk), .Reset(Impulse), .Number_of_tics(5'b00111), .Tics_out(main_1_tics_out));
  Shift_Register #(.width(24)) shift_register_1 (
    .shift(1'b1), .in(Input_line), .clk(main_1_tics_out), .out(Register_out), .clr(Reset), .q0(O0), .q1(O1),
    .q2(O2), .q3(O3), .q4(O4), .q5(O5), .q6(O6), .q7(O7));  // open: load, d0, d1, d2, d3, d4, d5, d6, d7

  assign Clk_out = Clk;
endmodule
