// Logisim project Skin_selectAND.circ as structural Verilog: 1 circuit, main circuit main
module main (
  input  _0,
  input  _1,
  input  _2,
  output [1:0] out
);

  wire or_1_out, or_2_out;
  wire [1:0] register_1_q, register_2_q;

  or or_1 (or_1_out, _0, _2);
  or or_2 (or_2_out, _0, _1);
  Register #(.width(2)) register_1 (.D(2'b01), .Q(register_1_q), .clk(_1), .clr(or_1_out));  // open: en
  Register #(.width(2)) register_2 (.D(2'b10), .Q(register_2_q), .clk(_2), .clr(or_2_out));  // open: en
  assign out = register_1_q | register_2_q;  // OR_Gate or_3, 2 bits wide
endmodule
