// Logisim project Timberman_or_tree_8_ROMs.circ as structural Verilog: 1 circuit, main circuit main
module main (
  input  [23:0] Input,
  input  Animation_Clock,
  input  Key_impulse,
  input  Reset__tree,
  input  [1:0] Register_address,
  input  Key_selection,
  output [23:0] Out_0,
  output [23:0] Out_1,
  output [23:0] Out_2,
  output [23:0] Out_3,
  output [23:0] Out_4,
  output [23:0] Out_5,
  output [23:0] Out_6,
  output [23:0] Out_7
);

  wire [23:0] _0, _1, _2, _3, _4, _5, _6, _7, main_1_o0, main_1_o1, main_1_o2, main_1_o3, main_1_o4,
       main_1_o5, main_1_o6, main_1_o7, multiplexer_1_out, multiplexer_2_out, multiplexer_3_out,
       multiplexer_4_out, multiplexer_5_out, multiplexer_6_out, multiplexer_7_out, multiplexer_8_out,
       rom_1_data, rom_2_data, rom_3_data, rom_4_data, rom_5_data, rom_6_data, rom_7_data, rom_8_data;

  Screen_animation_segment_main main_1 (
    .Input_line(Input), .Impulse(Key_impulse), .Reset(Reset__tree), .O0(main_1_o0), .O1(main_1_o1),
    .O2(main_1_o2), .O3(main_1_o3), .O4(main_1_o4), .O5(main_1_o5), .O6(main_1_o6), .O7(main_1_o7),
    .Clk(Animation_Clock));  // open: Register_out, Clk_out
  ROM #(.addrWidth(2), .dataWidth(24)) rom_1 (.addr(Register_address), .data(rom_1_data));  // open: sel
  ROM #(.addrWidth(2), .dataWidth(24)) rom_2 (.addr(Register_address), .data(rom_2_data));  // open: sel
  ROM #(.addrWidth(2), .dataWidth(24)) rom_3 (.addr(Register_address), .data(rom_3_data));  // open: sel
  ROM #(.addrWidth(2), .dataWidth(24)) rom_4 (.addr(Register_address), .data(rom_4_data));  // open: sel
  ROM #(.addrWidth(2), .dataWidth(24)) rom_5 (.addr(Register_address), .data(rom_5_data));  // open: sel
  ROM #(.addrWidth(2), .dataWidth(24)) rom_6 (.addr(Register_address), .data(rom_6_data));  // open: sel
  ROM #(.addrWidth(2), .dataWidth(24)) rom_7 (.addr(Register_address), .data(rom_7_data));  // open: sel
  ROM #(.addrWidth(2), .dataWidth(24)) rom_8 (.addr(Register_address), .data(rom_8_data));  // open: sel
  Multiplexer #(.width(24)) multiplexer_1 (
    .in0(rom_1_data), .in1(_0), .out(multiplexer_1_out), .sel(Key_selection));  // open: en
  Multiplexer #(.width(24)) multiplexer_2 (
    .in0(rom_2_data), .in1(_1), .out(multiplexer_2_out), .sel(Key_selection));  // open: en
  Multiplexer #(.width(24)) multiplexer_3 (
    .in0(rom_3_data), .in1(_2), .out(multiplexer_3_out), .sel(Key_selection));  // open: en
  Multiplexer #(.width(24)) multiplexer_4 (
    .in0(rom_4_data), .in1(_3), .out(multiplexer_4_out), .sel(Key_selection));  // open: en
  Multiplexer #(.width(24)) multiplexer_5 (
    .in0(rom_5_data), .in1(_4), .out(multiplexer_5_out), .sel(Key_selection));  // open: en
  Multiplexer #(.width(24)) multiplexer_6 (
    .in0(rom_6_data), .in1(_5), .out(multiplexer_6_out), .sel(Key_selection));  // open: en
  Multiplexer #(.width(24)) multiplexer_7 (
    .in0(rom_7_data), .in1(_6), .out(multiplexer_7_out), .sel(Key_selection));  // open: en
  Multiplexer #(.width(24)) multiplexer_8 (
    .in0(rom_8_data), .in1(_7), .out(multiplexer_8_out), .sel(Key_selection));  // open: en
  assign Out_0 = main_1_o0 | multiplexer_1_out;  // OR_Gate or_1, 24 bits wide
  assign Out_1 = main_1_o1 | multiplexer_2_out;  // OR_Gate or_2, 24 bits wide
  assign Out_2 = main_1_o2 | multiplexer_3_out;  // OR_Gate or_3, 24 bits wide
  assign Out_3 = main_1_o3 | multiplexer_4_out;  // OR_Gate or_4, 24 bits wide
  assign Out_4 = main_1_o4 | multiplexer_5_out;  // OR_Gate or_5, 24 bits wide
  assign Out_5 = main_1_o5 | multiplexer_6_out;  // OR_Gate or_6, 24 bits wide
  assign Out_6 = main_1_o6 | multiplexer_7_out;  // OR_Gate or_7, 24 bits wide
  assign Out_7 = main_1_o7 | multiplexer_8_out;  // OR_Gate or_8, 24 bits wide
  ROM #(.addrWidth(2), .dataWidth(24)) rom_9 (.addr(Register_address), .data(_0));  // open: sel
  ROM #(.addrWidth(2), .dataWidth(24)) rom_10 (.addr(Register_address), .data(_1));  // open: sel
  ROM #(.addrWidth(2), .dataWidth(24)) rom_11 (.addr(Register_address), .data(_2));  // open: sel
  ROM #(.addrWidth(2), .dataWidth(24)) rom_12 (.addr(Register_address), .data(_3));  // open: sel
  ROM #(.addrWidth(2), .dataWidth(24)) rom_13 (.addr(Register_address), .data(_4));  // open: sel
  ROM #(.addrWidth(2), .dataWidth(24)) rom_14 (.addr(Register_address), .data(_5));  // open: sel
  ROM #(.addrWidth(2), .dataWidth(24)) rom_15 (.addr(Register_address), .data(_6));  // open: sel
  ROM #(.addrWidth(2), .dataWidth(24)) rom_16 (.addr(Register_address), .data(_7));  // open: sel

  // Other names for the same wires on the sheet: Address[1:0] = Register_address

  // Notes on the sheet:
  //   contents of rom_1 (hex, n*v repeats v):
  //   0 320000 540000
  //   contents of rom_2 (hex, n*v repeats v):
  //   300000 7a0000 fc0000
  //   contents of rom_3 (hex, n*v repeats v):
  //   330000 320000 540000
  //   contents of rom_4 (hex, n*v repeats v):
  //   7b0000 7a0000 6c0000
  //   contents of rom_5 (hex, n*v repeats v):
  //   7e0000 7f0000 f80000
  //   contents of rom_6 (hex, n*v repeats v):
  //   720000 720000 ff0000
  //   contents of rom_7 (hex, n*v repeats v):
  //   300000 300000 780000
  //   contents of rom_8 (hex, n*v repeats v):
  //   cc0000 cc0000 480000
  //   contents of rom_9 (hex, n*v repeats v):
  //   0 4c 2a
  //   contents of rom_10 (hex, n*v repeats v):
  //   c 5e 3f
  //   contents of rom_11 (hex, n*v repeats v):
  //   cc 4c 2a
  //   contents of rom_12 (hex, n*v repeats v):
  //   de 5e 36
  //   contents of rom_13 (hex, n*v repeats v):
  //   7e fe 1f
  //   contents of rom_14 (hex, n*v repeats v):
  //   4e 4e ff
  //   contents of rom_15 (hex, n*v repeats v):
  //   c c 1e
  //   contents of rom_16 (hex, n*v repeats v):
  //   33 33 12
endmodule
