// Logisim project Timberman_or_tree_disp.circ as structural Verilog: 1 circuit, main circuit main
module main (
  input  [23:0] Register_in,
  input  Clk,
  input  in_3,
  input  in_4,
  input  [23:0] Timber_in,
  input  in_6,
  input  [2:0] Counter,
  output [23:0] O0,
  output [23:0] O1,
  output [23:0] out_10,
  output [23:0] out_11,
  output [23:0] out_12,
  output [23:0] out_13,
  output [23:0] out_14,
  output Disp_ready,
  output [23:0] O7
);

  wire [23:0] main_1_o0, main_1_o1, main_1_o2, main_1_o3, main_1_o4, main_1_o5, main_1_o6, main_1_o7,
       main_2_o1, main_2_o2, main_2_o2_2, main_2_o2_3, main_2_o2_4, main_2_o2_5, main_2_o2_6, main_2_o2_7;

  Screen_animation_segment_main main_1 (
    .Input_line(Register_in), .Impulse(in_3), .Reset(in_4), .O0(main_1_o0), .O1(main_1_o1), .O2(main_1_o2),
    .O3(main_1_o3), .O4(main_1_o4), .O5(main_1_o5), .O6(main_1_o6), .O7(main_1_o7), .Clk(Clk));  // open: Register_out, Clk_out
  Display_first_segment_control_main main_2 (
    .In(Timber_in), .Clk(Clk), .Reset(in_6), .Counter(Counter), .O1(main_2_o1), .O2(main_2_o2),
    .O2_2(main_2_o2_2), .O2_3(main_2_o2_3), .O2_4(main_2_o2_4), .O2_5(main_2_o2_5), .O2_6(main_2_o2_6),
    .O2_7(main_2_o2_7), .Display_ready(Disp_ready));
  assign O0 = main_1_o0 | main_2_o1;  // OR_Gate or_1, 24 bits wide
  assign O1 = main_1_o1 | main_2_o2;  // OR_Gate or_2, 24 bits wide
  assign out_10 = main_1_o2 | main_2_o2_2;  // OR_Gate or_3, 24 bits wide
  assign out_11 = main_1_o3 | main_2_o2_3;  // OR_Gate or_4, 24 bits wide
  assign out_12 = main_1_o4 | main_2_o2_4;  // OR_Gate or_5, 24 bits wide
  assign out_13 = main_1_o5 | main_2_o2_5;  // OR_Gate or_6, 24 bits wide
  assign out_14 = main_1_o6 | main_2_o2_6;  // OR_Gate or_7, 24 bits wide
  assign O7 = main_1_o7 | main_2_o2_7;  // OR_Gate or_8, 24 bits wide

  // Other names for the same wires on the sheet: Clk1 = Clk
endmodule
