// Logisim project gameboy.circ as structural Verilog: 1 circuit, main circuit main
module main (
  input  START,
  input  SKIN1,
  input  SKIN2,
  input  SKIN3,
  input  [6:0] KEY_out,
  input  KEYBOARD_2R,
  output [3:0] out_7,
  output [3:0] out_8,
  output [3:0] out_9,
  output [3:0] out_10,
  output [3:0] out_11,
  output [3:0] out_12,
  output [3:0] out_13,
  output [3:0] out_14,
  output [23:0] out_15,
  output [23:0] out_16,
  output [23:0] out_17,
  output [23:0] out_18,
  output [23:0] out_19,
  output Start_indicator,
  output [23:0] out_21,
  output [23:0] out_22,
  output [23:0] out_23,
  output [23:0] out_24,
  output [23:0] out_25,
  output [23:0] out_26,
  output [23:0] out_27,
  output [23:0] out_28,
  output [23:0] out_29,
  output [23:0] out_30,
  output [23:0] out_31,
  output [23:0] out_32,
  output [23:0] out_33,
  output [23:0] out_34,
  output [23:0] out_35,
  output [23:0] out_36,
  output [23:0] out_37,
  output [23:0] out_38,
  output [23:0] out_39,
  output [23:0] out_40,
  output [23:0] out_41,
  output [23:0] out_42,
  output [23:0] out_43,
  output [23:0] out_44,
  output [23:0] out_45,
  output [23:0] out_46,
  output [23:0] out_47,
  output [23:0] out_48,
  output [23:0] out_49,
  output [23:0] out_50,
  output [23:0] out_51,
  output [23:0] out_52,
  output [23:0] out_53,
  output [23:0] out_54,
  output CLK_KEYBOARD,
  output [23:0] out_56,
  output KEYBOARD_L1,
  output KEYBOARD_L2,
  output out_59,
  output out_60,
  output out_61,
  output out_62,
  output out_63,
  output out_64,
  output out_65,
  output out_66,
  output out_67,
  output out_68,
  output out_69,
  output out_70,
  output out_71,
  output out_72,
  output out_73,
  output out_74,
  output out_75,
  output out_76,
  output out_77,
  output out_78,
  output out_79,
  output out_80,
  output out_81,
  output out_82,
  output out_83,
  output out_84,
  output out_85,
  output out_86,
  output out_87,
  output out_88,
  output out_89,
  output out_90
);

  wire A, and_1_out, button_2_out, CLK_ANIM, CLK_IN, clock_1_out, comparator_2_eq, D, d_ff_1_q, d_ff_1_qn,
       d_ff_2_qn, d_ff_3_q, Key_impulse, main_2_clk_out, main_3_clk_out, main_4_clk_out, main_5_clk_out,
       main_8_clk_timebar, Main_clk_out, not_2_out, or_1_out, or_2_out, or_3_out, RESET, RstRgr, Scored,
       TIMEOUT;
  wire [1:0] key, main_1_out;
  wire [2:0] bit_extender_1_out, Counter, divider_1_rem, Kolizja_tree, random_1_out, shift_register_1_out,
       SR1, SR2, SR3, SR4, SR5;
  wire [13:0] Points_value;
  wire [23:0] main_2_register_out, main_3_reg_out, main_4_register_out, main_5_reg_out, RegOut, ROM0, ROM1,
       ROM2, ROM_3, ROM_4;

  Clock clock_1 (.out(clock_1_out));
  or or_1 (or_1_out, Key_impulse, RstRgr);
  Skin_selectAND_main main_1 (._0(SKIN1), ._1(SKIN2), ._2(SKIN3), .out(main_1_out));
  Random #(.width(3)) random_1 (.clk(clock_1_out), .out(random_1_out));  // open: next, clr
  Screen_animation_segment_main main_2 (
    .Input_line(RegOut), .Impulse(Key_impulse), .Reset(RstRgr), .O0(out_15), .O1(out_16), .O2(out_17),
    .Register_out(main_2_register_out), .O3(out_18), .O4(out_19), .O5(out_21), .O6(out_22), .O7(out_23),
    .Clk_out(main_2_clk_out), .Clk(CLK_ANIM));
  Over_screen_main main_3 (
    .Animation_Clock(main_2_clk_out), .Key_impulse(Key_impulse), .Reset__tree(RstRgr), .Out_0(out_24),
    .Out_1(out_25), .Out_2(out_26), .Out_3(out_27), .Out_4(out_28), .Out_5(out_29), .Out_6(out_30),
    .Out_7(out_31), .Input(main_2_register_out), .in_5(RstRgr), .Clk_out(main_3_clk_out),
    .Reg_out(main_3_reg_out));
  Screen_animation_segment_main main_4 (
    .Input_line(main_3_reg_out), .Impulse(Key_impulse), .Reset(RstRgr), .O0(out_32), .O1(out_33),
    .O2(out_34), .Register_out(main_4_register_out), .O3(out_35), .O4(out_36), .O5(out_37), .O6(out_38),
    .O7(out_39), .Clk_out(main_4_clk_out), .Clk(main_3_clk_out));
  Game_screen_main main_5 (
    .Animation_Clock(main_4_clk_out), .Key_impulse(Key_impulse), .Reset__tree(RstRgr), .Out_0(out_40),
    .Out_1(out_41), .Out_2(out_42), .Out_3(out_43), .Out_4(out_44), .Out_5(out_45), .Out_6(out_46),
    .Out_7(out_47), .Input(main_4_register_out), .in_5(RstRgr), .Clk_out(main_5_clk_out),
    .Reg_out(main_5_reg_out));
  Timberman_or_tree_8_ROMs_main main_6 (
    .Animation_Clock(main_5_clk_out), .Key_impulse(1'b1), .Reset__tree(or_1_out),
    .Register_address(main_1_out), .Out_0(out_48), .Out_1(out_49), .Out_2(out_50), .Out_3(out_51),
    .Out_4(out_52), .Out_5(out_53), .Out_6(out_54), .Out_7(out_56), .Input(main_5_reg_out), .Key_selection(D));
  Divider #(.width(3)) divider_1 (.a(random_1_out), .b(3'b011), .rem(divider_1_rem));  // open: out, upper
  Button button_1 (.out(RESET));
  Shift_Register #(.width(3), .length(5)) shift_register_1 (
    .in(divider_1_rem), .clk(KEYBOARD_L1), .out(shift_register_1_out), .clr(RstRgr), .q0(SR1), .q1(SR2),
    .q2(SR3), .q3(SR4), .q4(SR5));  // open: shift, load, d0, d1, d2, d3, d4
  or or_2 (or_2_out, RESET, RstRgr);
  TIMEDISPLAY_main main_7 (
    .WHEN_1__SUB_TIME_ONE_TICK__WHEN_0_ADD_TIME_ON_TICK(Scored), .CLK(main_8_clk_timebar), .RESET(or_2_out),
    .OutputScreen({out_59, out_60, out_61, out_62, out_63, out_64, out_65, out_66, out_67, out_68, out_69, out_70, out_71, out_72, out_73, out_74, out_75, out_76, out_77, out_78, out_79, out_80, out_81, out_82, out_83, out_84, out_85, out_86, out_87, out_88, out_89, out_90}),
    .TIME_OUT(TIMEOUT));
  Dynamic_difficulty_control_main main_8 (
    .Points_value(Points_value), .Clk_timebar(main_8_clk_timebar), .Stop(d_ff_1_q));
  D_Flip_Flop d_ff_1 (.clk(START), .D(d_ff_1_qn), .Q(d_ff_1_q), .Qn(d_ff_1_qn));  // open: preset, en, reset
  Shift_Register #(.width(3), .length(1)) shift_register_2 (
    .in(shift_register_1_out), .clk(KEYBOARD_L1), .out(Kolizja_tree), .clr(Key_impulse));  // open: shift, load, d0, q0
  Stop_countera_main main_9 (.Clk(CLK_ANIM), .Reset(Key_impulse), .Counter(Counter));
  Comparator #(.width(3)) comparator_1 (.a(Counter), .b(3'b000), .eq(KEYBOARD_L1));  // open: gt, lt
  assign bit_extender_1_out = {{1{1'b0}}, key};  // Bit_Extender bit_extender_1
  not not_1 (KEYBOARD_L2, KEYBOARD_L1);
  Pull_Resistor pull_resistor_1 (.node(CLK_KEYBOARD));
  assign CLK_KEYBOARD = KEYBOARD_2R ? CLK_IN : 1'bz;  // Controlled_Buffer controlled_buffer_1
  or or_3 (or_3_out, RESET, RstRgr);
  Comparator #(.width(3)) comparator_2 (
    .a(bit_extender_1_out), .b(Kolizja_tree), .eq(comparator_2_eq));  // open: gt, lt
  and and_1 (and_1_out, KEYBOARD_L1, comparator_2_eq);
  Button button_2 (.out(button_2_out));
  not not_2 (not_2_out, comparator_2_eq);
  ROM_Tree_main main_10 (.Counter(Counter), .ROM_0(ROM0), .ROM_1(ROM1), .ROM_2(ROM2), .ROM_3(ROM_3), .ROM_4(ROM_4));
  Shift_register_rom_control_main main_11 (
    .in_1(ROM0), .in_2(ROM1), .in_3(ROM2), .in_4(ROM_3), .in_5(ROM_4), .Output(RegOut), .Address(SR1));  // open: in_6, in_7, in_8
  PointCounter_main main_12 (
    .ADD(Scored), .RESET(or_3_out), .X000(out_11), ._0X00(out_12), ._00X0(out_13), ._000X(out_14),
    .Points(Points_value));  // open: LIMIT
  and and_2 (Scored, not_2_out, KEYBOARD_L1);
  Clock Main_clk (.out(Main_clk_out));
  D_Flip_Flop d_ff_2 (.clk(START), .D(d_ff_2_qn), .Q(Start_indicator), .Qn(d_ff_2_qn));  // open: preset, en, reset
  ScoreHolder_main main_13 (
    .CurrentPoints(Points_value), .CLK(CLK_IN), .X000(out_7), ._0X00(out_8), ._00X0(out_9), ._000X(out_10));  // open: RESET
  D_Flip_Flop d_ff_3 (.clk(TIMEOUT), .D(TIMEOUT), .Q(d_ff_3_q), .reset(Key_impulse));  // open: Qn, preset, en
  Clock #(.highDuration(4), .lowDuration(4)) Animation_clk (.out(CLK_ANIM));
  and and_3 (CLK_IN, Main_clk_out, Start_indicator);
  Key_recognition_main main_14 (
    .Keyboard_input(KEY_out), .Out(key), .Clk(CLK_IN), .A(A), .D(D), .KeyImpulse(Key_impulse));
  or or_4 (RstRgr, and_1_out, d_ff_3_q, button_2_out);

  // Other names for the same wires on the sheet: Alien = SKIN3; Display_ready = KEYBOARD_L1; H1[3:0] = out_14;
  //   H2[3:0] = out_13; H3[3:0] = out_12; H4[3:0] = out_11; HS1[3:0] = out_10; HS2[3:0] = out_9; HS3[3:0] = out_8;
  //   HS4[3:0] = out_7; linia1 = START; Start_Stop = START; Napoleon = SKIN2; Timber = SKIN1;
  //   Timer[31:0] = {out_59, out_60, out_61, out_62, out_63, out_64, out_65, out_66, out_67, out_68, out_69, out_70, out_71, out_72, out_73, out_74, out_75, out_76, out_77, out_78, out_79, out_80, out_81, out_82, out_83, out_84, out_85, out_86, out_87, out_88, out_89, out_90}

  // Notes on the sheet:
  //   Sekcja wyświetlania oparta na rejestrach przesuwnych
  //   Licznik pozostałego czasu gry
  //   Losowanie następnego segmentu drzewa
  //   oraz informacja do obsługi kolizji
  //   Najwyższy wynik
  //   Obecny wynik
  //   Iterowanie po ROMie
  //   System kolizji
  //   Segment start/stop
  //   Segment klawiatury oraz wybór skinów
  //   Wyświetlanie segmentów drzewa
  //   Licznik punktów
endmodule
