// Logisim project timberman.circ as structural Verilog: 1 circuit, main circuit main
module main (
);

  wire keyboard_1_avail, Kosmita_out, main_1_clk_keyboard, main_1_keyboard_l1, main_1_keyboard_l2,
       main_1_out_59, main_1_out_60, main_1_out_61, main_1_out_62, main_1_out_63, main_1_out_64,
       main_1_out_65, main_1_out_66, main_1_out_67, main_1_out_68, main_1_out_69, main_1_out_70,
       main_1_out_71, main_1_out_72, main_1_out_73, main_1_out_74, main_1_out_75, main_1_out_76,
       main_1_out_77, main_1_out_78, main_1_out_79, main_1_out_80, main_1_out_81, main_1_out_82,
       main_1_out_83, main_1_out_84, main_1_out_85, main_1_out_86, main_1_out_87, main_1_out_88,
       main_1_out_89, main_1_out_90, main_1_start_indicator, Napoleon_out, Standard_out, Start_stop_out;
  wire [3:0] H1, H2, H3, H4, main_1_out_11, main_1_out_12, main_1_out_13, main_1_out_14;
  wire [6:0] keyboard_1_data;
  wire [23:0] main_1_out_15, main_1_out_16, main_1_out_17, main_1_out_18, main_1_out_19, main_1_out_21,
       main_1_out_22, main_1_out_23, main_1_out_24, main_1_out_25, main_1_out_26, main_1_out_27,
       main_1_out_28, main_1_out_29, main_1_out_30, main_1_out_31, main_1_out_32, main_1_out_33,
       main_1_out_34, main_1_out_35, main_1_out_36, main_1_out_37, main_1_out_38, main_1_out_39,
       main_1_out_40, main_1_out_41, main_1_out_42, main_1_out_43, main_1_out_44, main_1_out_45,
       main_1_out_46, main_1_out_47, main_1_out_48, main_1_out_49, main_1_out_50, main_1_out_51,
       main_1_out_52, main_1_out_53, main_1_out_54, main_1_out_56;

  // Probe on main_1_start_indicator
  Button Start_stop (.out(Start_stop_out));
  Hex_Digit_Display hex_digit_display_1 (.value(H4));  // open: dp
  Hex_Digit_Display hex_digit_display_2 (.value(H3));  // open: dp
  Hex_Digit_Display hex_digit_display_3 (.value(main_1_out_11));  // open: dp
  Hex_Digit_Display hex_digit_display_4 (.value(main_1_out_12));  // open: dp
  Button Standard (.out(Standard_out));
  Button Napoleon (.out(Napoleon_out));
  Button Kosmita (.out(Kosmita_out));
  Hex_Digit_Display hex_digit_display_5 (.value(H1));  // open: dp
  Hex_Digit_Display hex_digit_display_6 (.value(H2));  // open: dp
  Hex_Digit_Display hex_digit_display_7 (.value(main_1_out_13));  // open: dp
  Hex_Digit_Display hex_digit_display_8 (.value(main_1_out_14));  // open: dp
  DotMatrix #(.matrixcols(32), .matrixrows(1)) dotmatrix_1 (
    .col0(main_1_out_59), .col1(main_1_out_60), .col2(main_1_out_61), .col3(main_1_out_62),
    .col4(main_1_out_63), .col5(main_1_out_64), .col6(main_1_out_65), .col7(main_1_out_66),
    .col8(main_1_out_67), .col9(main_1_out_68), .col10(main_1_out_69), .col11(main_1_out_70),
    .col12(main_1_out_71), .col13(main_1_out_72), .col14(main_1_out_73), .col15(main_1_out_74),
    .col16(main_1_out_75), .col17(main_1_out_76), .col18(main_1_out_77), .col19(main_1_out_78),
    .col20(main_1_out_79), .col21(main_1_out_80), .col22(main_1_out_81), .col23(main_1_out_82),
    .col24(main_1_out_83), .col25(main_1_out_84), .col26(main_1_out_85), .col27(main_1_out_86),
    .col28(main_1_out_87), .col29(main_1_out_88), .col30(main_1_out_89), .col31(main_1_out_90));
  gameboy_main main_1 (
    .START(Start_stop_out), .KEY_out(keyboard_1_data), .out_15(main_1_out_15), .out_16(main_1_out_16),
    .out_17(main_1_out_17), .out_18(main_1_out_18), .out_19(main_1_out_19), .out_21(main_1_out_21),
    .out_22(main_1_out_22), .out_23(main_1_out_23), .out_24(main_1_out_24), .out_25(main_1_out_25),
    .out_26(main_1_out_26), .out_27(main_1_out_27), .out_28(main_1_out_28), .out_29(main_1_out_29),
    .out_30(main_1_out_30), .out_31(main_1_out_31), .out_32(main_1_out_32), .out_33(main_1_out_33),
    .out_34(main_1_out_34), .out_35(main_1_out_35), .out_36(main_1_out_36), .out_37(main_1_out_37),
    .out_38(main_1_out_38), .out_39(main_1_out_39), .out_40(main_1_out_40), .out_41(main_1_out_41),
    .out_42(main_1_out_42), .out_43(main_1_out_43), .out_44(main_1_out_44), .out_45(main_1_out_45),
    .out_46(main_1_out_46), .out_47(main_1_out_47), .out_48(main_1_out_48), .out_49(main_1_out_49),
    .out_50(main_1_out_50), .out_51(main_1_out_51), .out_52(main_1_out_52), .out_53(main_1_out_53),
    .out_54(main_1_out_54), .out_56(main_1_out_56), .CLK_KEYBOARD(main_1_clk_keyboard),
    .KEYBOARD_2R(keyboard_1_avail), .KEYBOARD_L1(main_1_keyboard_l1), .KEYBOARD_L2(main_1_keyboard_l2),
    .out_7(H4), .out_11(main_1_out_11), .out_8(H3), .out_12(main_1_out_12), .out_9(H2),
    .out_13(main_1_out_13), .out_10(H1), .out_14(main_1_out_14), .out_59(main_1_out_59),
    .out_60(main_1_out_60), .out_61(main_1_out_61), .out_62(main_1_out_62), .out_63(main_1_out_63),
    .out_64(main_1_out_64), .out_65(main_1_out_65), .out_66(main_1_out_66), .out_67(main_1_out_67),
    .out_68(main_1_out_68), .out_69(main_1_out_69), .out_70(main_1_out_70), .out_71(main_1_out_71),
    .out_72(main_1_out_72), .out_73(main_1_out_73), .out_74(main_1_out_74), .out_75(main_1_out_75),
    .out_76(main_1_out_76), .out_77(main_1_out_77), .out_78(main_1_out_78), .out_79(main_1_out_79),
    .out_80(main_1_out_80), .out_81(main_1_out_81), .out_82(main_1_out_82), .out_83(main_1_out_83),
    .out_84(main_1_out_84), .out_85(main_1_out_85), .out_86(main_1_out_86), .out_87(main_1_out_87),
    .out_88(main_1_out_88), .out_89(main_1_out_89), .out_90(main_1_out_90), .SKIN1(Standard_out),
    .SKIN2(Napoleon_out), .SKIN3(Kosmita_out), .Start_indicator(main_1_start_indicator));
  Keyboard keyboard_1 (
    .clk(main_1_clk_keyboard), .re(main_1_keyboard_l1), .clr(main_1_keyboard_l2), .avail(keyboard_1_avail),
    .data(keyboard_1_data));
  DotMatrix #(.inputtype("row"), .matrixcols(24), .matrixrows(8)) dotmatrix_2 (
    .row0(main_1_out_15), .row1(main_1_out_16), .row2(main_1_out_17), .row3(main_1_out_18),
    .row4(main_1_out_19), .row5(main_1_out_21), .row6(main_1_out_22), .row7(main_1_out_23));
  DotMatrix #(.inputtype("row"), .matrixcols(24), .matrixrows(32)) dotmatrix_3 (
    .row0(main_1_out_24), .row1(main_1_out_25), .row2(main_1_out_26), .row3(main_1_out_27),
    .row4(main_1_out_28), .row5(main_1_out_29), .row6(main_1_out_30), .row7(main_1_out_31),
    .row8(main_1_out_32), .row9(main_1_out_33), .row10(main_1_out_34), .row11(main_1_out_35),
    .row12(main_1_out_36), .row13(main_1_out_37), .row14(main_1_out_38), .row15(main_1_out_39),
    .row16(main_1_out_40), .row17(main_1_out_41), .row18(main_1_out_42), .row19(main_1_out_43),
    .row20(main_1_out_44), .row21(main_1_out_45), .row22(main_1_out_46), .row23(main_1_out_47),
    .row24(main_1_out_48), .row25(main_1_out_49), .row26(main_1_out_50), .row27(main_1_out_51),
    .row28(main_1_out_52), .row29(main_1_out_53), .row30(main_1_out_54), .row31(main_1_out_56));
  Button A ();  // open: out
  Button D ();  // open: out

  // Notes on the sheet:
  //   0 - zegar wyłączony
  //   1 - zegar włączony
  //   Start gry
  //   Najwyższy wynik
  //   Wybór skina
  //   Sterowanie
  //   Rekomendowana częstotliwość tick frequency to 256 Hz
  //   Rekomendowana częstotliwość dla trybu trudnego to 512 Hz
  //   Przed rozpoczęciem gry należy załączyć zasilanie, klikając przysik Start/stop.
  //   Sonda nad przyciskiem musi wskazywać "1"
  //   Sterowanie postacią przy pomocy klawiatury.
  //   Po osiągnięciu 50 punktów zegar przyspieszy.
  //   Po osiągnięciu 100 jeszcze bardziej. Powodzenia
endmodule
